# Fritzing sketch BT0417C_setup (saved by Fritzing 0.8.7b)
breadboards: 1

parts:
  Part1 = Arduino Uno (Rev3)
  RHT1 = Humidity and Temperature Sensor RHT03

nets:
  N1: Part1.D2, RHT1.Data-signal
  N2: Part1.D3_PWM, RHT1.Vcc
  N3: Part1.5V, RHT1.GND_2
  N4: Part1.GND, RHT1.GND_1
